// Logisim project SevenSegDec.circ as structural Verilog: 1 circuit, main circuit SevenSegDec
module SevenSegDec (
  input  A3,
  input  A2,
  input  A1,
  input  A0,
  output S0,
  output S1,
  output S2,
  output S3,
  output S4,
  output S5,
  output S6
);

  wire and_1_out, and_2_out, and_3_out, and_4_out, and_5_out, and_6_out, and_7_out, and_8_out, and_9_out,
       not_1_out, not_2_out, not_3_out, not_4_out, not_5_out, not_6_out, not_7_out, not_8_out, not_9_out,
       not_10_out, not_11_out, not_12_out, not_13_out, not_14_out, not_15_out, not_16_out, not_17_out,
       not_18_out, not_19_out, not_20_out, not_21_out, not_22_out, not_23_out, or_1_out, or_2_out;

  not not_1 (not_1_out, A3);
  not not_2 (not_2_out, A2);
  not not_3 (not_3_out, A1);
  not not_4 (not_4_out, A3);
  not not_5 (not_5_out, A2);
  not not_6 (not_6_out, A0);
  not not_7 (not_7_out, A3);
  not not_8 (not_8_out, A2);
  not not_9 (not_9_out, A3);
  not not_10 (not_10_out, A1);
  not not_11 (not_11_out, A0);
  not not_12 (not_12_out, A3);
  not not_13 (not_13_out, A1);
  not not_14 (not_14_out, A3);
  not not_15 (not_15_out, A0);
  not not_16 (not_16_out, A3);
  not not_17 (not_17_out, A2);
  not not_18 (not_18_out, A1);
  not not_19 (not_19_out, A0);
  not not_20 (not_20_out, A3);
  not not_21 (not_21_out, A2);
  not not_22 (not_22_out, A1);
  not not_23 (not_23_out, A0);
  and and_1 (and_1_out, not_1_out, not_2_out, not_3_out, A0);
  and and_2 (and_2_out, not_4_out, not_5_out, A1, not_6_out);
  and and_3 (and_3_out, not_7_out, not_8_out, A1, A0);
  and and_4 (and_4_out, not_9_out, A2, not_10_out, not_11_out);
  and and_5 (and_5_out, not_12_out, A2, not_13_out, A0);
  and and_6 (and_6_out, not_14_out, A2, A1, not_15_out);
  and and_7 (and_7_out, not_16_out, A2, A1, A0);
  and and_8 (and_8_out, A3, not_17_out, not_18_out, not_19_out);
  and and_9 (and_9_out, not_20_out, not_21_out, not_22_out, not_23_out);
  or or_1 (or_1_out, and_2_out, and_5_out);
  or or_2 (or_2_out, and_3_out, and_6_out);
  or or_3 (S0, and_4_out, and_8_out, and_7_out, and_9_out);
  or or_4 (S1, or_2_out, and_7_out, and_8_out, and_4_out);
  or or_5 (S2, or_2_out, and_7_out, and_8_out, and_4_out, and_1_out);
  or or_6 (S3, or_1_out, and_8_out, or_2_out);
  _7_Segment_Display u_7_segment_display_1 (.g(S0), .f(S1), .a(S2), .b(S3), .e(S4), .d(S5), .c(S6));  // open: dp
  or or_7 (S4, or_2_out, and_8_out, and_4_out, and_1_out);
  or or_8 (S5, and_8_out, and_1_out, or_2_out, and_7_out, and_4_out, and_9_out);
  or or_9 (S6, and_8_out, and_9_out, or_2_out, and_7_out, and_4_out, or_1_out);

  // Notes on the sheet:
  //   Seven Segment Decoder
endmodule
